# Fritzing sketch hc05-design (saved by Fritzing 0.9.10b)

parts:
  Arduino_UNO = Arduino Uno (Rev3) - ICSP
  HC05_Bluetooth_Module = Bluetooth HC-05 Macho

nets:
  N1: Arduino_UNO.D0/RX, HC05_Bluetooth_Module.TXD
  N2: Arduino_UNO.D1/TX, HC05_Bluetooth_Module.RXD
  N3: Arduino_UNO.D2, HC05_Bluetooth_Module.Key
  5V: Arduino_UNO.5V, HC05_Bluetooth_Module.VCC
  GND: Arduino_UNO.GND, HC05_Bluetooth_Module.GND
