# Fritzing sketch design_schematic (saved by Fritzing 1.0.0d)

parts:
  Part1 = Arduino Uno (Rev3) - ICSP  # not connected
  M1 = gear-motor
  M2 = gear-motor
  M3 = gear-motor
  M4 = gear-motor
  A1 = Adafruit v1.2 motor shield
  Part2 = Bluetooth HC-06 Macho
  VCC1 = Battery  # not connected
  VCC2 = Battery block 9V  # not connected
  J1 = Power Jack [package=power_jack_pth]  # not connected

nets:
  N1: M1.pin_1, A1.Pin_48
  N2: M1.pin_2, A1.Pin_47
  N3: M2.pin_1, A1.Pin_2
  N4: M2.pin_2, A1.Pin_1
  N5: M3.pin_1, A1.Pin_5
  N6: M4.pin_1, A1.Pin_45
  N7: M4.pin_2, A1.Pin_44
  N8: A1.Pin_10, Part2.VCC
  N9: A1.Pin_11, A1.Pin_12, Part2.GND
  N10: A1.Pin_49, Part2.TXD
  N11: A1.Pin_50, Part2.RXD

notes:
  Motor Shield HAT
  Motor Shield Power Source
  Arduino Uno Power Supply
  HC06 Bluetooth Module
  Motor 1
  Motor 2
  Motor 3
  Motor 4
  Arduino Uno

custom parts:
  Adafruit v1.2 motor shield: Adafruit v1.2 motor shield.
